// Logisim project 8BitAddOrSubtract.circ as structural Verilog: 1 circuit, main circuit main
module main (
  input  [7:0] B_Values,
  input  A_Values,
  input  [7:0] in_3,
  input  Carry_In,
  input  in_5,
  output [7:0] Sum_2_x
);

  wire A_p2, A_p4, main_1_p2, main_1_p3, main_1_p4, main_2_p1, main_3_p2, main_3_p4, main_4_p1, main_4_p3,
       main_5_p8, main_5_p9, main_5_p10, main_6_p4, main_7_p3;

  // Full_Adder_main A: pin names not known; wires that end beside it: B_Values[7], A_p2, in_5, A_p4, Sum_2_x[7], B_Values[6]
  // Full_Adder_main main_1: pin names not known; wires that end beside it: B_Values[5], main_1_p2, main_1_p3, main_1_p4, Sum_2_x[5]
  // Full_Adder_main main_2: pin names not known; wires that end beside it: main_2_p1, A_p4, main_1_p3, Sum_2_x[6]
  // Full_Adder_main main_3: pin names not known; wires that end beside it: B_Values[4], main_3_p2, main_1_p4, main_3_p4, Sum_2_x[4], B_Values[3]
  // Full_Adder_main main_4: pin names not known; wires that end beside it: main_4_p1, main_3_p4, main_4_p3, Sum_2_x[3]
  // One_s_Compliment_main main_5: pin names not known; wires that end beside it: in_3, A_Values, A_p2, main_2_p1, main_1_p2, main_3_p2, main_4_p1, main_5_p8, main_5_p9, main_5_p10
  // Full_Adder_main main_6: pin names not known; wires that end beside it: B_Values[2], main_5_p8, main_4_p3, main_6_p4, Sum_2_x[2], B_Values[1]
  // Full_Adder_main main_7: pin names not known; wires that end beside it: main_5_p9, main_6_p4, main_7_p3, Sum_2_x[1]
  // Full_Adder_main main_8: pin names not known; wires that end beside it: B_Values[0], main_5_p10, main_7_p3, Carry_In, Sum_2_x[0]

  // Notes on the sheet:
  //   A
  //   FA
  //   FA
  //   Carry Out
  //   0-Subtract, 1-Add
  //   FA
  //   FA
  //   FA
  //   FA
  //   7 6 5 4 3 2 1 0
  //   FA
  //   CO
  //   S
  //   Full Adder
  //   One's Compliment
endmodule
