// Logisim project 8BitAdder.circ as structural Verilog: 1 circuit, main circuit main
module main (
  input  [1:0] in_1,
  input  [1:0] in_2,
  input  [1:0] in_3,
  input  [1:0] in_4,
  input  [1:0] in_5,
  input  [1:0] in_6,
  input  [1:0] A,
  input  [1:0] B,
  input  CI,
  input  in_10,
  output [7:0] S
);

  wire A_p4, main_1_p3, main_1_p4, main_3_p3, main_4_p3, main_5_p3, main_5_p4;

  // Full_Adder_main A: pin names not known; wires that end beside it: in_1[1], in_1[0], in_10, A_p4, S[7]
  // Full_Adder_main main_1: pin names not known; wires that end beside it: in_3[1], in_3[0], main_1_p3, main_1_p4, S[5], in_4[1]
  // Full_Adder_main main_2: pin names not known; wires that end beside it: in_2[1], in_2[0], A_p4, main_1_p3, S[6]
  // Full_Adder_main main_3: pin names not known; wires that end beside it: in_4[0], main_1_p4, main_3_p3, S[4], in_5[1]
  // Full_Adder_main main_4: pin names not known; wires that end beside it: in_5[0], main_3_p3, main_4_p3, S[3], in_6[1]
  // Full_Adder_main main_5: pin names not known; wires that end beside it: A[1], A[0], main_5_p3, main_5_p4, S[1], B[1]
  // Full_Adder_main main_6: pin names not known; wires that end beside it: in_6[0], main_4_p3, main_5_p3, S[2]
  // Full_Adder_main main_7: pin names not known; wires that end beside it: B[0], main_5_p4, CI, S[0]

  // Notes on the sheet:
  //   A
  //   7 6 5 4 3 2 1 0
  //   CO
  //   S
  //   Full Adder
endmodule
