// Logisim project One'sCompliment.circ as structural Verilog: 1 circuit, main circuit main
module main (
  input  [7:0] in_1,
  input  in_2,
  output out_3,
  output out_4,
  output out_5,
  output out_6,
  output out_7,
  output out_8,
  output out_9,
  output out_10
);

  wire not_1_out;

  not not_1 (not_1_out, in_2);
  xor xor_1 (out_4, not_1_out, in_1[6]);
  xor xor_2 (out_3, not_1_out, in_1[7]);
  xor xor_3 (out_6, not_1_out, in_1[4]);
  xor xor_4 (out_5, not_1_out, in_1[5]);
  xor xor_5 (out_8, not_1_out, in_1[2]);
  xor xor_6 (out_7, not_1_out, in_1[3]);
  xor xor_7 (out_9, not_1_out, in_1[1]);
  xor xor_8 (out_10, not_1_out, in_1[0]);
endmodule
