// Logisim project FullAdder.circ as structural Verilog: 1 circuit, main circuit main
module main (
  input  in_1,
  input  in_2,
  input  in_3,
  output out_4,
  output out_5
);

  wire main_1_p3, main_1_p4, main_2_p4;

  // Half_Adder_main main_1: pin names not known; wires that end beside it: in_2, in_3, main_1_p3, main_1_p4
  // Half_Adder_main main_2: pin names not known; wires that end beside it: in_1, main_1_p3, out_4, main_2_p4
  or or_1 (out_5, main_2_p4, main_1_p4);
endmodule
